// Logisim project TinyCPU-AddArithmeticCircuit.circ as structural Verilog: 1 circuit, main circuit AddArithmeticCircuit
module AddArithmeticCircuit (
  input  [15:0] LEFT,
  input  [15:0] RIGHT,
  input  INPUT_VALID,
  output [15:0] RESULT,
  output OVERFLOW,
  output RESULT_VALID
);

  wire NO_OVERFLOW_out, OPERAND_SIGN_DIFFERENT_out, OPERAND_SIGN_SAME_out, RESULT_SIGN_CHANGED_out;

  Adder #(.width(16)) ADDER (.a(LEFT), .b(RIGHT), .out(RESULT));  // open: cin, cout
  // XOR_Gate OPERAND_SIGN_DIFFERENT has open pins: out=OPERAND_SIGN_DIFFERENT_out
  not OPERAND_SIGN_SAME (OPERAND_SIGN_SAME_out, OPERAND_SIGN_DIFFERENT_out);
  // XOR_Gate RESULT_SIGN_CHANGED has open pins: out=RESULT_SIGN_CHANGED_out
  and SIGN_OVERFLOW (OVERFLOW, OPERAND_SIGN_SAME_out, RESULT_SIGN_CHANGED_out);
  not NO_OVERFLOW (NO_OVERFLOW_out, OVERFLOW);
  and RANGE_VALID (RESULT_VALID, NO_OVERFLOW_out, INPUT_VALID);

  // Notes on the sheet:
  //   signed ADD: overflow = NOT(left_sign XOR right_sign) AND (left_sign XOR result_sign)
endmodule
