// Logisim project TinyCPU-AddSub.circ as structural Verilog: 1 circuit, main circuit AddSub
module AddSub (
  input  [31:0] OPERANDS,
  input  SUBTRACT,
  input  [1:0] VALID,
  output CARRY,
  output [15:0] RESULT,
  output RESULT_VALID
);

  wire BOTH_VALID_out;
  wire [15:0] ADDER_out, SUBTRACTOR_out;

  Adder #(.width(16)) ADDER (.a(OPERANDS[15:0]), .b(OPERANDS[31:16]), .out(ADDER_out), .cin(1'b1), .cout(CARRY));
  Subtractor #(.width(16)) SUBTRACTOR (
    .a(OPERANDS[15:0]), .b(OPERANDS[31:16]), .out(SUBTRACTOR_out));  // open: bin, bout
  and BOTH_VALID (BOTH_VALID_out, VALID[0], VALID[1]);
  and ACTIVE_VALID (RESULT_VALID, SUBTRACT, BOTH_VALID_out);
  Multiplexer #(.width(16)) MULTIPLEXER (.in0(ADDER_out), .in1(SUBTRACTOR_out), .out(RESULT), .sel(SUBTRACT));

  // Notes on the sheet:
  //   ADD / SUB — gebündelte Operanden- und Validitätsbusse
endmodule
