// Logisim project TinyCPU-AddSubCircuit.circ as structural Verilog: 1 circuit, main circuit AddSubCircuit
module AddSubCircuit (
  input  DEFAULT_VALID,
  input  MEMORY_VALID,
  input  ACC_VALID,
  input  NOT_VALID_SELECT,
  input  ADD_ADDRESS,
  input  ADD_ADDRESS_REGISTER,
  input  ADD_ADDRESS_REGISTER_PLUS_OFFSET,
  input  ADD_CONST,
  output ADD_VALID
);

  wire ACC_ADD_MEMORY_SELECT_out, ACC_ADD_SELECT_out, ACC_ADD_VALID_out, MULTIPLEXER_2_out,
       MULTIPLEXER_3_out, MULTIPLEXER_out;

  or ACC_ADD_MEMORY_SELECT (ACC_ADD_MEMORY_SELECT_out, ADD_ADDRESS, ADD_ADDRESS_REGISTER, ADD_ADDRESS_REGISTER_PLUS_OFFSET);
  or ACC_ADD_SELECT (ACC_ADD_SELECT_out, ACC_ADD_MEMORY_SELECT_out, ADD_CONST);
  Multiplexer MULTIPLEXER (.in0(1'b1), .in1(DEFAULT_VALID), .out(MULTIPLEXER_out), .sel(ACC_ADD_MEMORY_SELECT_out));
  buf ACC_ADD_VALID (ACC_ADD_VALID_out, ACC_VALID);  // AND_Gate
  Multiplexer MULTIPLEXER_2 (.in0(1'b1), .in1(DEFAULT_VALID), .out(MULTIPLEXER_2_out), .sel(MEMORY_VALID));
  Multiplexer MULTIPLEXER_3 (.in0(MULTIPLEXER_2_out), .in1(ACC_VALID), .out(MULTIPLEXER_3_out), .sel(NOT_VALID_SELECT));
  Multiplexer MULTIPLEXER_4 (
    .in0(MULTIPLEXER_3_out), .in1(ACC_ADD_VALID_out), .out(ADD_VALID), .sel(ACC_ADD_SELECT_out));

  // Notes on the sheet:
  //   ADD_ADDRESS/CONST_VALID →
  //   CONST_VALID →
  //   ADD_SELECT →
  //   ADD_OPERAND_VALID →
  //   MEMORY_VALID →
  //   ADD_VALID →
  //   DEFAULT_VALID →
  //   ADD_VALID →
  //   MEMORY_VALID →
  //   NOT_SELECT →
  //   ALU_VALID →
  //   ALU_VALID →
  //   ALU_VALID →
endmodule
