// Logisim project TinyCPU-AddressPath.circ as structural Verilog: 1 circuit, main circuit AddressPath
module AddressPath (
  input  [11:0] ADDRESS_IN,
  input  AR_LOAD,
  input  [11:0] OFFSET,
  input  VALID_IN,
  input  CLK,
  output [11:0] ADDRESS,
  output [11:0] ADDRESS_PLUS_OFFSET,
  output OFFSET_CARRY,
  output ADDRESS_VALID
);

  wire [15:12] AR_q, undriven;

  Register #(.width(16)) AR (.D({undriven, ADDRESS_IN}), .en(AR_LOAD), .clk(CLK), .Q({AR_q, ADDRESS}));  // open: clr
  Register #(.width(1)) AR_VALID (.D(VALID_IN), .en(AR_LOAD), .clk(CLK), .Q(ADDRESS_VALID));  // open: clr
  Adder #(.width(12)) OFFSET_ADDER (
    .a(ADDRESS), .b(OFFSET), .out(ADDRESS_PLUS_OFFSET), .cout(OFFSET_CARRY));  // open: cin
  // Pins of 12 and 16 bits meet at {undriven, ADDRESS_IN}
  // Pins of 12 and 16 bits meet at {AR_q, ADDRESS}

  // Notes on the sheet:
  //   Clocked 12-bit address register with combinational offset addition
endmodule
