// Logisim project TinyCPU-ErrorFlags.circ as structural Verilog: 1 circuit, main circuit ErrorFlags
module ErrorFlags (
  input  CLEAR_ERROR,
  input  CLK,
  input  SET_OVF,
  input  SET_DIV0,
  input  SET_ADDR,
  input  SET_INV,
  input  SET_ILL,
  input  SET_INPUT,
  output OVF_OUT,
  output DIV0_OUT,
  output ADDR_OUT,
  output INV_OUT,
  output ILL_OUT,
  output INPUT_OUT
);

  wire HOLD_ADDR_out, HOLD_DIV0_out, HOLD_ILL_out, HOLD_INPUT_out, HOLD_INV_out, HOLD_OVF_out, NEXT_ADDR_out,
       NEXT_DIV0_out, NEXT_ILL_out, NEXT_INPUT_out, NEXT_INV_out, NEXT_OVF_out, NOT_CLEAR_ERROR_out;

  not NOT_CLEAR_ERROR (NOT_CLEAR_ERROR_out, CLEAR_ERROR);
  and HOLD_OVF (HOLD_OVF_out, OVF_OUT, NOT_CLEAR_ERROR_out);
  and HOLD_DIV0 (HOLD_DIV0_out, DIV0_OUT, NOT_CLEAR_ERROR_out);
  and HOLD_ADDR (HOLD_ADDR_out, ADDR_OUT, NOT_CLEAR_ERROR_out);
  and HOLD_INV (HOLD_INV_out, INV_OUT, NOT_CLEAR_ERROR_out);
  and HOLD_ILL (HOLD_ILL_out, ILL_OUT, NOT_CLEAR_ERROR_out);
  and HOLD_INPUT (HOLD_INPUT_out, INPUT_OUT, NOT_CLEAR_ERROR_out);
  or NEXT_OVF (NEXT_OVF_out, SET_OVF, HOLD_OVF_out);
  or NEXT_DIV0 (NEXT_DIV0_out, SET_DIV0, HOLD_DIV0_out);
  or NEXT_ADDR (NEXT_ADDR_out, SET_ADDR, HOLD_ADDR_out);
  or NEXT_INV (NEXT_INV_out, SET_INV, HOLD_INV_out);
  or NEXT_ILL (NEXT_ILL_out, SET_ILL, HOLD_ILL_out);
  or NEXT_INPUT (NEXT_INPUT_out, SET_INPUT, HOLD_INPUT_out);
  // Register #(.width(1)) OVF: pin names not known; wires that end beside it: NEXT_OVF_out, CLK, NEXT_DIV0_out, CLK, OVF_OUT, DIV0_OUT
  // Register #(.width(1)) DIV0: pin names not known; wires that end beside it: NEXT_DIV0_out, CLK, NEXT_ADDR_out, CLK, DIV0_OUT, ADDR_OUT
  // Register #(.width(1)) ADDR: pin names not known; wires that end beside it: NEXT_ADDR_out, CLK, NEXT_INV_out, CLK, ADDR_OUT, INV_OUT
  // Register #(.width(1)) INV: pin names not known; wires that end beside it: NEXT_INV_out, CLK, NEXT_ILL_out, CLK, INV_OUT, ILL_OUT
  // Register #(.width(1)) ILL: pin names not known; wires that end beside it: NEXT_ILL_out, CLK, NEXT_INPUT_out, CLK, ILL_OUT, INPUT_OUT
  // Register #(.width(1)) INPUT: pin names not known; wires that end beside it: NEXT_INPUT_out, CLK, INPUT_OUT

  // Notes on the sheet:
  //   Set-dominant sticky flags: SET OR (current AND NOT CLEAR_ERROR)
endmodule
