// Logisim project TinyCPU-FetchDecode.circ as structural Verilog: 1 circuit, main circuit FetchDecode
module FetchDecode (
  input  DEC_JUMP_NOT_ZERO,
  input  NOT_ZERO,
  input  CLK,
  input  RESET,
  input  [15:0] PROGRAM_LIMIT,
  input  DEC_HALT_ERROR,
  output LOAD_CONST,
  output LOAD_ADDRESS,
  output JUMP_NOT_ZERO,
  output LOAD_ADDRESS_REGISTER,
  output LOAD_ADDRESS_REGISTER_PLUS_OFFSET,
  output ADD_CONST,
  output ADD_ADDRESS,
  output HALT_ERROR,
  output ADD_ADDRESS_REGISTER,
  output ADD_ADDRESS_REGISTER_PLUS_OFFSET,
  output SUB_CONST,
  output SUB_ADDRESS,
  output SUB_ADDRESS_REGISTER,
  output SUB_ADDRESS_REGISTER_PLUS_OFFSET,
  output [11:0] PC_OUT,
  output MUL_CONST,
  output MUL_ADDRESS,
  output MUL_ADDRESS_REGISTER,
  output MUL_ADDRESS_REGISTER_PLUS_OFFSET,
  output DIV_CONST,
  output DIV_ADDRESS,
  output DIV_ADDRESS_REGISTER,
  output [21:0] OPCODE,
  output DIV_ADDRESS_REGISTER_PLUS_OFFSET,
  output AND_CONST,
  output AND_ADDRESS,
  output AND_ADDRESS_REGISTER,
  output AND_ADDRESS_REGISTER_PLUS_OFFSET,
  output OR_CONST,
  output OR_ADDRESS,
  output OR_ADDRESS_REGISTER,
  output OR_ADDRESS_REGISTER_PLUS_OFFSET,
  output STORE_ADDRESS,
  output [15:0] Address,
  output STORE_ADDRESS_REGISTER,
  output STORE_ADDRESS_REGISTER_PLUS_OFFSET,
  output LOAD_ADDRESS_REGISTER_CONST,
  output LOAD_ADDRESS_REGISTER_ADDRESS,
  output NOT,
  output JUMP_ADDRESS,
  output JUMP_ZERO,
  output JUMP_NEGATIVE,
  output JUMP_ERROR,
  output JUMP_NOT_ERROR,
  output CLEAR_ERROR,
  output INPUT,
  output PRINT,
  output PRINT_ADDRESS,
  output HALT,
  output out_56,
  output SET_OVF,
  output SET_DIV0,
  output SET_ADDR,
  output SET_INV,
  output SET_ILL,
  output SET_INPUT
);

  wire comparator_1_eq;
  wire [15:0] adder_1_out;
  wire [15:12] PC_q;

  Register #(.width(16)) PC (.D(adder_1_out), .clk(CLK), .Q({PC_q, PC_OUT}), .clr(RESET));  // open: en
  Comparator #(.width(16)) comparator_1 (.a(PROGRAM_LIMIT), .b({PC_q, PC_OUT}), .eq(comparator_1_eq));  // open: gt, lt
  Adder #(.width(16)) adder_1 (.a({PC_q, PC_OUT}), .b({16{1'b1}}), .out(adder_1_out));  // open: cin, cout
  ROM #(.addrWidth(12), .dataWidth(22)) INSTRUCTION_ROM (.addr(PC_OUT), .data({OPCODE[21:16], Address}));
  and JNZ_TAKEN (JUMP_NOT_ZERO, DEC_JUMP_NOT_ZERO, NOT_ZERO);
  or ERROR_HALT (HALT_ERROR, comparator_1_eq, DEC_HALT_ERROR);
  Decoder #(.select(6)) decoder_1 (
    .out0(LOAD_CONST), .out1(LOAD_ADDRESS), .out2(LOAD_ADDRESS_REGISTER),
    .out3(LOAD_ADDRESS_REGISTER_PLUS_OFFSET), .out4(ADD_CONST), .out5(ADD_ADDRESS),
    .out6(ADD_ADDRESS_REGISTER), .out7(ADD_ADDRESS_REGISTER_PLUS_OFFSET), .out8(SUB_CONST),
    .out9(SUB_ADDRESS), .out10(SUB_ADDRESS_REGISTER), .out11(SUB_ADDRESS_REGISTER_PLUS_OFFSET),
    .out12(MUL_CONST), .out13(MUL_ADDRESS), .out14(MUL_ADDRESS_REGISTER),
    .out15(MUL_ADDRESS_REGISTER_PLUS_OFFSET), .out16(DIV_CONST), .out17(DIV_ADDRESS),
    .out18(DIV_ADDRESS_REGISTER), .out19(DIV_ADDRESS_REGISTER_PLUS_OFFSET), .out20(AND_CONST),
    .out21(AND_ADDRESS), .out22(AND_ADDRESS_REGISTER), .out23(AND_ADDRESS_REGISTER_PLUS_OFFSET),
    .out24(OR_CONST), .out25(OR_ADDRESS), .out26(OR_ADDRESS_REGISTER),
    .out27(OR_ADDRESS_REGISTER_PLUS_OFFSET), .out28(STORE_ADDRESS), .out29(STORE_ADDRESS_REGISTER),
    .out30(STORE_ADDRESS_REGISTER_PLUS_OFFSET), .out31(LOAD_ADDRESS_REGISTER_CONST),
    .out32(LOAD_ADDRESS_REGISTER_ADDRESS), .out33(NOT), .out34(JUMP_ADDRESS), .out35(JUMP_ZERO),
    .out36(JUMP_NEGATIVE), .out37(JUMP_ERROR), .out38(JUMP_NOT_ERROR), .out39(CLEAR_ERROR), .out40(INPUT),
    .out41(PRINT), .out42(PRINT_ADDRESS), .out43(HALT), .out44(out_56), .out45(SET_OVF), .out46(SET_DIV0),
    .out47(SET_ADDR), .out48(SET_INV), .out49(SET_ILL), .out50(SET_INPUT), .sel(OPCODE[21:16]));  // open: out51, out52, out53, out54, out55, out56, out57, out58, out59, out60, out61, out62, out63, en

  assign OPCODE[15:0] = Address;

  // Notes on the sheet:
  //   PROGRAM_LIMIT: initial=0xfff
  //   AP 7 machine format v1: stable six-bit opcode allocation and encoder-generated ROM
  //   contents of INSTRUCTION_ROM (hex, n*v repeats v):
  //   3fffff 65 3 64 0 65 64 4
endmodule
