// Logisim project TinyCPU-FetchDecode1.circ as structural Verilog: 1 circuit, main circuit FetchDecode
module FetchDecode (
  input  CLK,
  input  ZERO,
  input  RESET,
  input  [15:0] PROGRAM_LIMIT,
  output ERROR,
  output [11:0] PC_OUT,
  output [21:0] INSTRUCTION
);

  wire [15:0] adder_1_out;
  wire [15:12] PC_q;

  Register #(.width(16)) PC (.D(adder_1_out), .clk(CLK), .Q({PC_q, PC_OUT}), .clr(RESET));  // open: en
  Comparator #(.width(16)) comparator_1 (.a(PROGRAM_LIMIT), .b({PC_q, PC_OUT}), .eq(ERROR));  // open: gt, lt
  Adder #(.width(16)) adder_1 (.a({PC_q, PC_OUT}), .b({16{1'b1}}), .out(adder_1_out));  // open: cin, cout
  ROM #(.addrWidth(12), .dataWidth(22)) INSTRUCTION_ROM (.addr(PC_OUT), .data(INSTRUCTION));

  // Notes on the sheet:
  //   PROGRAM_LIMIT: initial=0xfff
  //   AP 7 machine format v1: stable six-bit opcode allocation and encoder-generated ROM
  //   contents of INSTRUCTION_ROM (hex, n*v repeats v):
  //   ffff 1c0065 3 1c0064 2a0000 50065 1c0064 240004 2c0000
endmodule
