// Logisim project TinyCPU-FetchDecode2.circ as structural Verilog: 1 circuit, main circuit FetchDecode2
module FetchDecode2 (
  input  DEC_JUMP_NOT_ZERO,
  input  NOT_ZERO,
  input  ERROR,
  input  DEC_HALT_ERROR,
  output JUMP_NOT_ZERO,
  output HALT_ERROR
);

  and JNZ_TAKEN (JUMP_NOT_ZERO, DEC_JUMP_NOT_ZERO, NOT_ZERO);
  or ERROR_HALT (HALT_ERROR, ERROR, DEC_HALT_ERROR);

  // Notes on the sheet:
  //   FetchDecode part 2 keeps only processed control signals; direct pass-through pins are omitted.
endmodule
