// Logisim project TinyCPU-FetchDecode3.circ as structural Verilog: 1 circuit, main circuit FetchDecode
module FetchDecode (
  input  [5:0] OPCODE,
  output LOAD_ADDRESS,
  output LOAD_ADDRESS_REGISTER,
  output LOAD_ADDRESS_REGISTER_PLUS_OFFSET,
  output ADD_CONST,
  output ADD_ADDRESS_REGISTER,
  output ADD_ADDRESS_REGISTER_PLUS_OFFSET,
  output SUB_CONST,
  output SUB_ADDRESS,
  output SUB_ADDRESS_REGISTER,
  output SUB_ADDRESS_REGISTER_PLUS_OFFSET,
  output MUL_CONST,
  output MUL_ADDRESS,
  output MUL_ADDRESS_REGISTER,
  output MUL_ADDRESS_REGISTER_PLUS_OFFSET,
  output DIV_CONST,
  output DIV_ADDRESS,
  output DIV_ADDRESS_REGISTER,
  output DIV_ADDRESS_REGISTER_PLUS_OFFSET,
  output AND_CONST,
  output AND_ADDRESS,
  output AND_ADDRESS_REGISTER,
  output AND_ADDRESS_REGISTER_PLUS_OFFSET,
  output OR_CONST,
  output OR_ADDRESS,
  output OR_ADDRESS_REGISTER,
  output OR_ADDRESS_REGISTER_PLUS_OFFSET,
  output STORE_ADDRESS_REGISTER,
  output STORE_ADDRESS_REGISTER_PLUS_OFFSET,
  output LOAD_ADDRESS_REGISTER_CONST,
  output LOAD_ADDRESS_REGISTER_ADDRESS,
  output NOT,
  output JUMP_ADDRESS,
  output JUMP_ZERO,
  output JUMP_NEGATIVE,
  output JUMP_ERROR,
  output JUMP_NOT_ERROR,
  output CLEAR_ERROR,
  output INPUT,
  output PRINT_ADDRESS,
  output SET_OVF,
  output SET_DIV0,
  output SET_INV,
  output SET_ILL,
  output SET_INPUT
);

  // Decoder #(.select(6)) decoder_1: pin names not known; wires that end beside it: ADD_ADDRESS_REGISTER, ADD_ADDRESS_REGISTER_PLUS_OFFSET, SUB_CONST, SUB_ADDRESS, SUB_ADDRESS_REGISTER, SUB_ADDRESS_REGISTER_PLUS_OFFSET, MUL_CONST, MUL_ADDRESS, MUL_ADDRESS_REGISTER, MUL_ADDRESS_REGISTER_PLUS_OFFSET, DIV_CONST, DIV_ADDRESS, DIV_ADDRESS_REGISTER, DIV_ADDRESS_REGISTER_PLUS_OFFSET, AND_CONST, AND_ADDRESS, AND_ADDRESS_REGISTER, AND_ADDRESS_REGISTER_PLUS_OFFSET, OR_CONST, OR_ADDRESS, OR_ADDRESS_REGISTER, OR_ADDRESS_REGISTER_PLUS_OFFSET, STORE_ADDRESS_REGISTER, STORE_ADDRESS_REGISTER_PLUS_OFFSET, LOAD_ADDRESS_REGISTER_CONST, LOAD_ADDRESS_REGISTER_ADDRESS, NOT, JUMP_ADDRESS, JUMP_ZERO, JUMP_NEGATIVE, JUMP_ERROR, JUMP_NOT_ERROR, CLEAR_ERROR, OPCODE
endmodule
