// Logisim project TinyCPU-FetchDecodeControls.circ as structural Verilog: 1 circuit, main circuit FetchDecodeControls
module FetchDecodeControls (
  input  [5:0] OPCODE,
  output LOAD_CONST,
  output LOAD_ADR,
  output LOAD_ADR_REG,
  output LOAD_REG_OFF,
  output ADD_CONST,
  output ADD_ADR,
  output ADD_ADR_REG,
  output ADD_REG_OFF,
  output SUB_CONST,
  output SUB_ADR,
  output SUB_ADR_REG,
  output SUB_REG_OFF,
  output MUL_CONST,
  output MUL_ADR,
  output MUL_ADR_REG,
  output MUL_REG_OFF,
  output DIV_CONST,
  output DIV_ADR,
  output DIV_ADR_REG,
  output DIV_REG_OFF,
  output AND_CONST,
  output AND_ADR,
  output AND_ADR_REG,
  output AND_REG_OFF,
  output OR_CONST,
  output OR_ADR,
  output OR_ADR_REG,
  output OR_REG_OFF,
  output STORE_ADR,
  output STORE_ADR_REG,
  output STORE_REG_OFF,
  output LD_REG_CONST,
  output LD_REG_ADR,
  output NOT,
  output JUMP_ADR,
  output JUMP_ZERO,
  output JUMP_NEGATIVE,
  output JUMP_ERROR,
  output JUMP_NOT_ERROR,
  output CLEAR_ERROR,
  output INPUT,
  output PRINT,
  output PRINT_ADR,
  output HALT,
  output HALT_ERROR,
  output SET_OVF,
  output SET_DIV0,
  output SET_ADDR,
  output SET_INV,
  output SET_ILL,
  output SET_INPUT,
  output XOR_CONST,
  output XOR_ADR,
  output XOR_ADR_REG,
  output XOR_REG_OFF,
  output JUMP_NOT_ZERO
);

  wire decoder_1_out50;

  Decoder #(.select(6)) decoder_1 (
    .out0(LOAD_CONST), .out1(LOAD_ADR), .out2(LOAD_ADR_REG), .out3(LOAD_REG_OFF), .out4(ADD_CONST),
    .out5(ADD_ADR), .out6(ADD_ADR_REG), .out7(ADD_REG_OFF), .out8(SUB_CONST), .out9(SUB_ADR),
    .out10(SUB_ADR_REG), .out11(SUB_REG_OFF), .out12(MUL_CONST), .out13(MUL_ADR), .out14(MUL_ADR_REG),
    .out15(MUL_REG_OFF), .out16(DIV_CONST), .out17(DIV_ADR), .out18(DIV_ADR_REG), .out19(DIV_REG_OFF),
    .out20(AND_CONST), .out21(AND_ADR), .out22(AND_ADR_REG), .out23(AND_REG_OFF), .out24(OR_CONST),
    .out25(OR_ADR), .out26(OR_ADR_REG), .out27(OR_REG_OFF), .out28(STORE_ADR), .out29(STORE_ADR_REG),
    .out30(STORE_REG_OFF), .out31(LD_REG_CONST), .out32(LD_REG_ADR), .out33(NOT), .out34(JUMP_ADR),
    .out35(JUMP_ZERO), .out36(JUMP_NOT_ZERO), .out37(JUMP_NEGATIVE), .out38(JUMP_ERROR),
    .out39(JUMP_NOT_ERROR), .out40(CLEAR_ERROR), .out41(INPUT), .out42(PRINT), .out43(PRINT_ADR),
    .out44(HALT), .out45(HALT_ERROR), .out46(XOR_CONST), .out47(XOR_ADR), .out48(XOR_ADR_REG),
    .out49(XOR_REG_OFF), .out50(decoder_1_out50), .sel(OPCODE));  // open: out51, out52, out53, out54, out55, out56, out57, out58, out59, out60, out61, out62, out63, en

  assign SET_ADDR = 1'b0;
  assign SET_DIV0 = 1'b0;
  assign SET_ILL = 1'b0;
  assign SET_INPUT = 1'b0;
  assign SET_INV = 1'b0;
  assign SET_OVF = 1'b0;
endmodule
