// Logisim project TinyCPU-NotCircuit.circ as structural Verilog: 1 circuit, main circuit NotCircuit
module NotCircuit (
  input  [15:0] ACC_VALUE,
  input  ACC_VALID,
  input  NOT_SELECT,
  output [15:0] RESULT,
  output OVERFLOW,
  output NOT_VALID,
  output NOT_SELECTED
);

  assign RESULT = ~ACC_VALUE;  // NOT_Gate NOT_VALUE, 16 bits wide
  and ACTIVE_NOT_VALID (NOT_VALID, ACC_VALID, NOT_SELECT);

  assign NOT_SELECTED = NOT_SELECT;
  assign OVERFLOW = 1'b1;
endmodule
