// Logisim project TinyCPU-SubValidCircuit.circ as structural Verilog: 1 circuit, main circuit SubValidCircuit
module SubValidCircuit (
  input  SUB_ADDRESS,
  input  SUB_ADDRESS_REGISTER,
  input  SUB_ADDRESS_REGISTER_PLUS_OFFSET,
  input  SUB_CONST,
  input  MEMORY_VALID,
  input  ACC_VALID,
  output SUB_ACTIVE,
  output SUB_VALID
);

  wire ACC_SUB_MEMORY_SELECT_out, MULTIPLEXER_830_330_2_out;

  or ACC_SUB_MEMORY_SELECT (ACC_SUB_MEMORY_SELECT_out, SUB_ADDRESS, SUB_ADDRESS_REGISTER, SUB_ADDRESS_REGISTER_PLUS_OFFSET);
  or ACC_SUB_FAMILY_SELECT (SUB_ACTIVE, ACC_SUB_MEMORY_SELECT_out, SUB_CONST);
  Multiplexer MULTIPLEXER_830_330_2 (
    .in0(1'b1), .in1(MEMORY_VALID), .out(MULTIPLEXER_830_330_2_out), .sel(ACC_SUB_MEMORY_SELECT_out));
  and ACC_SUB_VALID (SUB_VALID, MULTIPLEXER_830_330_2_out, ACC_VALID);

  // Notes on the sheet:
  //   SUB_ADDRESS/CONST_VALID →
  //   SUB_OPERAND_VALID →
  //   SUB_VALID →
endmodule
